# Fritzing sketch Prototype (saved by Fritzing 0.9.2b)
circuit board: 3.67895cm x 8.67416cm
breadboards: 1

parts:
  Front_Sensor = HC-SR04
  Teensy_2_0 = Teensy 2.0
  Regulator_3_3v = Voltage Regulator - 3.3V [package="TO220 [THT]"]
  Left_Sensor = HC-SR04
  Right_sensor = HC-SR04
  part = ESP8266 WiFi Module [part_number=ESP8266]

nets:
  VCC: Front_Sensor.VCC, Teensy_2_0.VCC, Regulator_3_3v.input_voltage, Left_Sensor.VCC, Right_sensor.VCC
  N1: Front_Sensor.Trig, Teensy_2_0.F0
  N2: Front_Sensor.Echo, Teensy_2_0.F1
  GND: Front_Sensor.GND, Teensy_2_0.GND, Regulator_3_3v.GND, Left_Sensor.GND, Right_sensor.GND, part.GND
  N3: Teensy_2_0.D2, part.TXD
  N4: Teensy_2_0.D3, part.RXD
  N5: Teensy_2_0.F7, Right_sensor.Echo
  N6: Teensy_2_0.F6, Right_sensor.Trig
  N7: Teensy_2_0.F5, Left_Sensor.Echo
  N8: Teensy_2_0.F4, Left_Sensor.Trig
  N9: Regulator_3_3v.output_voltage, part.VCC, part.CH_PD

custom parts:
  HC-SR04: Ultrasonic ranging module HC - SR04 provides 2cm - 400cm non-contact measurement function, the ranging accuracy can reach to 3mm. The modules includes ultrasonic transmitters, receiver and control circuit
  Voltage Regulator - 3.3V: 3.3V DC Voltage Regulator
  ESP8266 WiFi Module: Generic WiFi Module based on the ESP8266 with onboard PCB antenna and UART communications
